// Logisim project SD_Group01.circ as structural Verilog: 7 circuits, main circuit main
module main (
  output [11:0] pc,
  output [11:0] r0,
  output [11:0] r1,
  output [11:0] r2,
  output [11:0] r3,
  output [11:0] r4,
  output [11:0] r5,
  output [11:0] r6,
  output [11:0] r7,
  output halt
);

  wire and_1_out, and_2_out, and_3_out, clock_1_out, control_1_addi, control_1_beq, control_1_blt,
       control_1_branch_absolute, control_1_branch_relative, control_1_funct_code_or_add,
       control_1_immediate_zonder_ldi, control_1_jal, control_1_jr, control_1_ldi,
       control_1_memory_to_register, control_1_opp_code_funct_als_alu_op, control_1_store, control_1_write,
       control_1_zero, not_1_out, or_1_out, or_2_out, or_3_out, or_4_out, or_5_out, reset_out;
  wire [2:0] bit_extender_1_out, decoder_1_rd, decoder_1_rs_000, multiplexer_5_out, multiplexer_6_out,
       multiplexer_8_out, multiplexer_9_out;
  wire [3:0] decoder_1_funct, decoder_1_opp_code, multiplexer_3_out, multiplexer_4_out, multiplexer_10_out,
       multiplexer_11_out, multiplexer_13_out;
  wire [11:0] bit_extender_2_out, controlled_buffer_1_out, decoder_1_branch_value_addi, decoder_1_immediate,
       decoder_1_jr, decoder_1_target_adress, multiplexer_1_out, multiplexer_2_out, multiplexer_7_out,
       multiplexer_12_out, multiplexer_14_out, multiplexer_15_out, multiplexer_18_out, n12_bit_alu_1_p2,
       n12_bit_alu_1_p4, register_file_1_p14, register_file_1_p16, register_file_1_p17;
  wire [15:0] ram_1_data;

  Multiplexer #(.width(12)) multiplexer_1 (
    .in0(decoder_1_target_adress), .in1(n12_bit_alu_1_p4), .out(multiplexer_1_out), .sel(control_1_jr));  // open: en
  Halt halt_1 (.instruction(ram_1_data), .clock(clock_1_out), .reset(reset_out), .halt(halt));
  Clock clock_1 (.out(clock_1_out));
  Button reset (.out(reset_out));
  and and_1 (and_1_out, and_3_out, control_1_branch_relative);
  Multiplexer #(.width(12)) multiplexer_2 (
    .in0(multiplexer_1_out), .in1(decoder_1_branch_value_addi), .out(multiplexer_2_out), .sel(and_3_out));  // open: en
  and and_2 (and_2_out, ~halt, clock_1_out);  // AND_Gate
  PC_block pc_block_1 (
    .Branch_relative(and_1_out), .Branch_absolute(control_1_branch_absolute),
    .Branch_value(multiplexer_2_out), .clock(and_2_out), .reset(reset_out), .PC(pc));
  and and_3 (and_3_out, or_1_out, n12_bit_alu_1_p4[0]);
  or or_1 (or_1_out, control_1_beq, control_1_blt);
  RAM_part #(.addrWidth(12), .dataWidth(16)) ram_1 (
    .addr(pc), .data(ram_1_data), .clk(and_2_out), .ld(1'b1));  // open: sel, clr
  decoder decoder_1 (
    .istruction(ram_1_data), .funct(decoder_1_funct), .rs_000(decoder_1_rs_000), .rd(decoder_1_rd),
    .opp_code(decoder_1_opp_code), .immediate(decoder_1_immediate), .target_adress(decoder_1_target_adress),
    .jr(decoder_1_jr), .branch_value_addi(decoder_1_branch_value_addi));
  control control_1 (
    .opp_code(decoder_1_opp_code), .functie_code(decoder_1_funct), .zero(control_1_zero),
    .opp_code_funct_als_alu_op(control_1_opp_code_funct_als_alu_op), .write(control_1_write),
    .immediate_zonder_ldi(control_1_immediate_zonder_ldi), .store(control_1_store),
    .memory_to_register(control_1_memory_to_register), .funct_code_or_add(control_1_funct_code_or_add),
    .ldi(control_1_ldi), .branch_relative(control_1_branch_relative),
    .branch_absolute(control_1_branch_absolute), .jal(control_1_jal), .jr(control_1_jr),
    .addi(control_1_addi), .beq(control_1_beq), .blt(control_1_blt));
  Bit_Extender #(.in_width(4), .out_width(3)) bit_extender_1 (.in(decoder_1_funct), .out(bit_extender_1_out));
  assign bit_extender_2_out = {{8{1'b0}}, decoder_1_funct};  // Bit_Extender bit_extender_2
  Multiplexer #(.width(4)) multiplexer_3 (
    .in0(decoder_1_opp_code), .in1(4'b0100), .out(multiplexer_3_out), .sel(control_1_funct_code_or_add));  // open: en
  Multiplexer #(.width(4)) multiplexer_4 (
    .in0(decoder_1_funct), .in1(4'b0100), .out(multiplexer_4_out), .sel(or_2_out));  // open: en
  or or_2 (or_2_out, control_1_jr, control_1_jal);
  or or_3 (or_3_out, control_1_beq, control_1_blt);
  Multiplexer #(.width(3)) multiplexer_5 (
    .in0(bit_extender_1_out), .in1(decoder_1_rs_000), .out(multiplexer_5_out), .sel(or_3_out));  // open: en
  Multiplexer #(.width(3)) multiplexer_6 (
    .in0(decoder_1_rd), .in1(3'b000), .out(multiplexer_6_out), .sel(control_1_zero));  // open: en
  Multiplexer #(.width(12)) multiplexer_7 (
    .in0(bit_extender_2_out), .in1(decoder_1_branch_value_addi), .out(multiplexer_7_out), .sel(control_1_addi));  // open: en
  or or_4 (or_4_out, control_1_jal, control_1_write);
  or or_5 (or_5_out, control_1_beq, control_1_blt, control_1_jr);
  Multiplexer #(.width(3)) multiplexer_8 (
    .in0(decoder_1_rs_000), .in1(multiplexer_9_out), .out(multiplexer_8_out), .sel(or_5_out));  // open: en
  Multiplexer #(.width(3)) multiplexer_9 (
    .in0(multiplexer_6_out), .in1(3'b111), .out(multiplexer_9_out), .sel(control_1_jal));  // open: en
  Multiplexer #(.width(4)) multiplexer_10 (
    .in0(multiplexer_3_out), .in1(multiplexer_4_out), .out(multiplexer_10_out),
    .sel(control_1_opp_code_funct_als_alu_op));  // open: en
  Multiplexer #(.width(4)) multiplexer_11 (
    .in0(multiplexer_10_out), .in1(4'b1000), .out(multiplexer_11_out), .sel(control_1_beq));  // open: en
  Multiplexer #(.width(12)) multiplexer_12 (
    .in0(multiplexer_15_out), .in1(decoder_1_jr), .out(multiplexer_12_out), .sel(control_1_jr));  // open: en
  Multiplexer #(.width(4)) multiplexer_13 (
    .in0(multiplexer_11_out), .in1(4'b0110), .out(multiplexer_13_out), .sel(control_1_blt));  // open: en
  // register_file register_file_1: pin names not known; wires that end beside it: r0, multiplexer_8_out, r1, multiplexer_5_out, r2, multiplexer_9_out, r3, or_4_out, r4, and_2_out, r5, reset_out, r6, register_file_1_p14, r7, register_file_1_p16, register_file_1_p17
  Multiplexer #(.width(12)) multiplexer_14 (
    .in0(register_file_1_p16), .in1(pc), .out(multiplexer_14_out), .sel(control_1_jal));  // open: en
  Multiplexer #(.width(12)) multiplexer_15 (
    .in0(register_file_1_p17), .in1(multiplexer_7_out), .out(multiplexer_15_out),
    .sel(control_1_immediate_zonder_ldi));  // open: en
  // _12_bit_ALU 12_bit_alu_1: pin names not known; wires that end beside it: multiplexer_14_out, n12_bit_alu_1_p2, multiplexer_13_out, n12_bit_alu_1_p4
  Multiplexer #(.width(12)) multiplexer_16 (
    .in0(multiplexer_18_out), .in1(decoder_1_immediate), .out(register_file_1_p14), .sel(control_1_ldi));  // open: en
  Multiplexer #(.width(12)) multiplexer_17 (
    .in0(multiplexer_12_out), .in1(12'h1), .out(n12_bit_alu_1_p2), .sel(control_1_jal));  // open: en
  assign controlled_buffer_1_out = control_1_store ? register_file_1_p16 : 12'bz;  // Controlled_Buffer controlled_buffer_1
  not not_1 (not_1_out, control_1_store);
  RAM_part #(.addrWidth(12), .dataWidth(12)) ram_2 (
    .addr(n12_bit_alu_1_p4), .data(controlled_buffer_1_out), .clk(and_2_out), .ld(not_1_out));  // open: sel, clr
  Multiplexer #(.width(12)) multiplexer_18 (
    .in0(n12_bit_alu_1_p4), .in1(controlled_buffer_1_out), .out(multiplexer_18_out),
    .sel(control_1_memory_to_register));  // open: en

  // Notes on the sheet:
  //   current instruction
  //   enkel branchen als relative en conditie voldaan
  //   branch/jump
  //   target/jr
  //   clock signal
  //   reset button
  //   opp code
  //   opp code
  //   functie code
  //   functie
  //   rt
  //   rs
  //   rd
  //   opp code or add
  //   bij JAL ook writen
  //   bij jr rs=rd
  //   rd/r7
  //   immediate
  //   DO NOT CHANGE THE INPUTS AND OUTPUTS OF THIS CIRCUIT! Do not add/remove inputs or outputs. Do not even change their location or orientation.
  //   clock
  //   write
  //   S
  //   T
  //   alu operation
  //   store data
  //   imm
  //   12 bit
  //   alu/ RAM uitkomst 
  //   mem to reg
endmodule

module Halt (
  input  [15:0] instruction,
  input  clock,
  input  reset,
  output halt
);

  wire and_1_out, comparator_1_eq, comparator_2_gt, counter_1_carry, or_1_out, or_2_out;
  wire [11:0] counter_1_q;

  Comparator #(.width(16), .mode("unsigned")) comparator_1 (
    .a(instruction), .b({16{1'b0}}), .eq(comparator_1_eq));  // open: gt, lt
  Counter #(.width(12), .max('hfff), .trigger("falling")) counter_1 (
    .Q(counter_1_q), .carry(counter_1_carry), .clk(clock), .clr(reset));  // open: load, D, count
  or or_1 (or_1_out, comparator_1_eq, counter_1_carry);
  Comparator #(.width(12), .mode("unsigned")) comparator_2 (
    .a(counter_1_q), .b({12{1'b0}}), .gt(comparator_2_gt));  // open: eq, lt
  or or_2 (or_2_out, halt, and_1_out);
  and and_1 (and_1_out, or_1_out, comparator_2_gt);
  Register #(.width(1)) register_1 (.D(or_2_out), .Q(halt), .clk(clock), .clr(reset));  // open: en

  // Notes on the sheet:
  //   halt becomes and stays asserted if the instruction is 0000 (not in the first clock cycle) or the end of the counter is reached (2^12)
endmodule

module Instruction_memory (
  input  [11:0] Adress,
  input  clock,
  output [15:0] instruction
);

  RAM_part #(.addrWidth(12), .dataWidth(16)) ram_1 (
    .addr(Adress), .data(instruction), .clk(clock), .ld(1'b1));  // open: sel, clr
endmodule

// PC
module PC_block (
  input  Branch_relative,
  input  Branch_absolute,
  input  [11:0] Branch_value,
  input  clock,
  input  reset,
  output [11:0] PC
);

  wire [11:0] multiplexer_1_out, multiplexer_2_out, n12_bit_lookahead_adder_1_p1,
       n12_bit_lookahead_adder_1_p2;

  Multiplexer #(.width(12)) multiplexer_1 (
    .in0(multiplexer_2_out), .in1(Branch_value), .out(multiplexer_1_out), .sel(Branch_absolute));  // open: en
  Multiplexer #(.width(12)) multiplexer_2 (
    .in0(n12_bit_lookahead_adder_1_p2), .in1(n12_bit_lookahead_adder_1_p1), .out(multiplexer_2_out),
    .sel(Branch_relative));  // open: en
  // _12_bit_lookahead_adder 12_bit_lookahead_adder_1: pin names not known; wires that end beside it: n12_bit_lookahead_adder_1_p1, n12_bit_lookahead_adder_1_p2, Branch_value, 1'b0
  // _12_bit_register 12_bit_register_1: pin names not known; wires that end beside it: clock, 1'b1, reset, multiplexer_1_out, PC
  // _12_bit_lookahead_adder 12_bit_lookahead_adder_2: pin names not known; wires that end beside it: n12_bit_lookahead_adder_1_p2, PC, 12'h1, 1'b0

  // Notes on the sheet:
  //   12-bit register
endmodule

module RAM (
  input  [11:0] store_data,
  input  store,
  input  [11:0] PC,
  input  Clock,
  output [11:0] Load_store_data
);

  wire not_1_out;

  assign Load_store_data = store ? store_data : 12'bz;  // Controlled_Buffer controlled_buffer_1
  not not_1 (not_1_out, store);
  RAM_part #(.addrWidth(12), .dataWidth(12)) ram_1 (
    .addr(PC), .data(Load_store_data), .clk(Clock), .ld(not_1_out));  // open: sel, clr
endmodule

module decoder (
  input  [15:0] istruction,
  output [3:0] funct,
  output [2:0] rs_000,
  output [2:0] rd,
  output [3:0] opp_code,
  output [11:0] immediate,
  output [11:0] jr,
  output [11:0] target_adress,
  output [11:0] branch_value_addi
);

  assign immediate = {{4{istruction[7]}}, istruction[7:0]};  // Bit_Extender bit_extender_1
  assign jr = {{8{istruction[7]}}, istruction[7:4]};  // Bit_Extender bit_extender_2
  assign target_adress = {{4{1'b0}}, istruction[11:4]};  // Bit_Extender bit_extender_3
  assign branch_value_addi = {{8{istruction[3]}}, istruction[3:0]};  // Bit_Extender bit_extender_4

  assign funct = istruction[3:0];
  assign opp_code = istruction[15:12];
  assign rd = istruction[10:8];
  assign rs_000 = istruction[6:4];
endmodule

module control (
  input  [3:0] opp_code,
  input  [3:0] functie_code,
  output zero,
  output opp_code_funct_als_alu_op,
  output write,
  output immediate_zonder_ldi,
  output store,
  output memory_to_register,
  output funct_code_or_add,
  output ldi,
  output branch_relative,
  output branch_absolute,
  output jr,
  output jal,
  output addi,
  output beq,
  output blt
);

  wire and_3_out, and_4_out, and_5_out, and_6_out, and_10_out, and_11_out, and_12_out, and_13_out,
       and_14_out, and_19_out;

  and and_1 (zero, ~opp_code[0], ~opp_code[1], ~opp_code[2], ~opp_code[3]);  // AND_Gate
  and and_2 (opp_code_funct_als_alu_op, opp_code[0], ~opp_code[1], ~opp_code[2], ~opp_code[3]);  // AND_Gate
  and and_3 (and_3_out, opp_code[0], opp_code[1], ~opp_code[2], opp_code[3]);  // AND_Gate
  and and_4 (and_4_out, ~opp_code[0], opp_code[1], ~opp_code[2], opp_code[3]);  // AND_Gate
  and and_5 (and_5_out, opp_code[0], opp_code[1], ~opp_code[2], opp_code[3]);  // AND_Gate
  and and_6 (and_6_out, opp_code[0], ~opp_code[1], opp_code[2], opp_code[3]);  // AND_Gate
  and and_7 (store, opp_code[0], opp_code[1], ~opp_code[2], opp_code[3]);  // AND_Gate
  and and_8 (memory_to_register, ~opp_code[0], opp_code[1], ~opp_code[2], opp_code[3]);  // AND_Gate
  and and_9 (ldi, ~opp_code[0], ~opp_code[1], opp_code[2], opp_code[3]);  // AND_Gate
  and and_10 (and_10_out, ~opp_code[0], opp_code[1], opp_code[2], opp_code[3]);  // AND_Gate
  and and_11 (and_11_out, opp_code[0], opp_code[1], opp_code[2], opp_code[3]);
  and and_12 (and_12_out, ~functie_code[0], functie_code[1], ~functie_code[2], ~functie_code[3]);  // AND_Gate
  and and_13 (and_13_out, functie_code[0], functie_code[1], ~functie_code[2], ~functie_code[3]);  // AND_Gate
  and and_14 (and_14_out, ~functie_code[0], ~functie_code[1], functie_code[2], ~functie_code[3]);  // AND_Gate
  and and_15 (addi, opp_code[0], ~opp_code[1], opp_code[2], opp_code[3]);  // AND_Gate
  and and_16 (beq, ~opp_code[0], opp_code[1], opp_code[2], opp_code[3]);  // AND_Gate
  and and_17 (blt, opp_code[0], opp_code[1], opp_code[2], opp_code[3]);
  and and_18 (jr, opp_code_funct_als_alu_op, and_12_out);
  and and_19 (and_19_out, opp_code_funct_als_alu_op, and_13_out);
  and and_20 (jal, opp_code_funct_als_alu_op, and_14_out);
  or or_1 (funct_code_or_add, and_4_out, and_5_out, and_6_out);
  or or_2 (branch_relative, and_10_out, and_11_out);
  and and_21 (write, ~and_3_out, ~jr, ~and_19_out, ~beq, ~blt);  // AND_Gate
  or or_3 (branch_absolute, jr, and_19_out, jal);

  assign immediate_zonder_ldi = funct_code_or_add;

  // Notes on the sheet:
  //   moet telkens ook de oppcode op0001
  //   write altijd buiten bij jr en j en branches
endmodule
